// Logisim project subtract.circ as structural Verilog: 1 circuit, main circuit main
module main (
  input  in_1,
  input  in_2,
  input  in_3,
  input  in_4,
  input  in_5,
  input  in_6,
  input  in_7,
  input  in_8,
  input  in_9,
  input  in_10,
  input  in_11,
  input  in_12,
  input  in_13,
  input  in_14,
  input  in_15,
  input  in_16,
  input  in_17,
  input  in_18,
  input  in_19,
  input  in_20,
  input  in_21,
  input  in_22,
  input  in_23,
  input  in_24,
  input  in_25,
  input  in_26,
  input  in_27,
  input  in_28,
  input  in_29,
  input  in_30,
  input  in_31,
  input  in_32,
  input  in_33,
  input  in_34,
  input  in_35,
  input  in_36,
  input  in_37,
  input  in_38,
  input  in_39,
  input  in_40,
  input  in_41,
  input  in_42,
  input  in_43,
  input  in_44,
  input  in_45,
  input  in_46,
  input  in_47,
  input  in_48,
  input  in_49,
  input  in_50,
  input  in_51,
  input  in_52,
  input  in_53,
  input  in_54,
  input  in_55,
  input  in_56,
  input  in_57,
  input  in_58,
  input  in_59,
  input  in_60,
  input  in_61,
  input  in_62,
  input  in_63,
  input  in_64,
  input  in_65,
  input  in_66,
  output out_67,
  output out_68,
  output out_69,
  output out_70,
  output out_71,
  output out_72,
  output out_73,
  output out_74,
  output out_75,
  output out_76,
  output out_77,
  output out_78,
  output out_79,
  output out_80,
  output out_81,
  output out_82,
  output out_83,
  output out_84,
  output out_85,
  output out_86,
  output out_87,
  output out_88,
  output out_89,
  output out_90,
  output out_91,
  output out_92,
  output out_93,
  output out_94,
  output out_95,
  output out_96,
  output out_97,
  output out_98,
  output out_99,
  output out_100
);

  wire and_1_out, and_2_out, and_3_out, and_4_out, and_5_out, and_6_out, and_7_out, and_8_out, and_9_out,
       and_10_out, and_11_out, and_12_out, and_13_out, and_14_out, and_15_out, and_16_out, and_17_out,
       and_18_out, and_19_out, and_20_out, and_21_out, and_22_out, and_23_out, and_24_out, and_25_out,
       and_26_out, and_27_out, and_28_out, and_29_out, and_30_out, and_31_out, and_32_out, and_33_out,
       and_34_out, and_35_out, and_36_out, and_37_out, and_38_out, and_39_out, and_40_out, and_41_out,
       and_42_out, and_43_out, and_44_out, and_45_out, and_46_out, and_47_out, and_48_out, and_49_out,
       and_50_out, and_51_out, and_52_out, and_53_out, and_54_out, and_55_out, and_56_out, and_57_out,
       and_58_out, and_59_out, and_60_out, and_61_out, and_62_out, and_63_out, and_64_out, or_1_out,
       or_2_out, or_3_out, or_4_out, or_5_out, or_6_out, or_7_out, or_8_out, or_9_out, or_10_out, or_11_out,
       or_12_out, or_13_out, or_14_out, or_15_out, or_16_out, or_17_out, or_18_out, or_19_out, or_20_out,
       or_21_out, or_22_out, or_23_out, or_24_out, or_25_out, or_26_out, or_27_out, or_28_out, or_29_out,
       or_30_out, or_31_out, xor_1_out, xor_2_out, xor_3_out, xor_4_out, xor_5_out, xor_6_out, xor_7_out,
       xor_8_out, xor_9_out, xor_11_out, xor_13_out, xor_15_out, xor_17_out, xor_18_out, xor_19_out,
       xor_20_out, xor_21_out, xor_22_out, xor_23_out, xor_24_out, xor_29_out, xor_30_out, xor_31_out,
       xor_32_out, xor_33_out, xor_35_out, xor_37_out, xor_39_out, xor_41_out, xor_42_out, xor_43_out,
       xor_44_out, xor_45_out, xor_46_out, xor_49_out, xor_51_out, xor_53_out, xor_54_out, xor_55_out,
       xor_56_out, xor_57_out, xor_59_out, xor_61_out, xor_63_out, xor_65_out, xor_66_out, xor_67_out,
       xor_68_out, xor_69_out, xor_71_out, xor_73_out, xor_75_out, xor_77_out, xor_78_out, xor_79_out,
       xor_80_out, xor_81_out, xor_83_out, xor_85_out, xor_87_out, xor_89_out, xor_90_out, xor_91_out,
       xor_92_out, xor_93_out;

  xor xor_1 (xor_1_out, in_2, in_5);
  xor xor_2 (xor_2_out, in_2, in_3);
  xor xor_3 (xor_3_out, in_2, in_20);
  xor xor_4 (xor_4_out, in_2, in_36);
  xor xor_5 (xor_5_out, in_2, in_52);
  xor xor_6 (xor_6_out, in_1, xor_2_out);
  and and_1 (and_1_out, xor_2_out, in_1);
  xor xor_7 (xor_7_out, in_19, xor_3_out);
  and and_2 (and_2_out, xor_3_out, in_19);
  xor xor_8 (xor_8_out, in_35, xor_4_out);
  and and_3 (and_3_out, xor_4_out, in_35);
  xor xor_9 (xor_9_out, in_51, xor_5_out);
  and and_4 (and_4_out, xor_5_out, in_51);
  and and_5 (and_5_out, xor_6_out, xor_1_out);
  and and_6 (and_6_out, xor_7_out, or_29_out);
  and and_7 (and_7_out, xor_8_out, or_30_out);
  and and_8 (and_8_out, xor_9_out, or_31_out);
  xor xor_10 (out_67, xor_6_out, xor_1_out);
  or or_1 (or_1_out, and_5_out, and_1_out);
  xor xor_11 (xor_11_out, in_2, in_8);
  xor xor_12 (out_75, xor_7_out, or_29_out);
  or or_2 (or_2_out, and_6_out, and_2_out);
  xor xor_13 (xor_13_out, in_2, in_24);
  xor xor_14 (out_83, xor_8_out, or_30_out);
  or or_3 (or_3_out, and_7_out, and_3_out);
  xor xor_15 (xor_15_out, in_2, in_40);
  xor xor_16 (out_91, xor_9_out, or_31_out);
  or or_4 (or_4_out, and_8_out, and_4_out);
  xor xor_17 (xor_17_out, in_2, in_56);
  xor xor_18 (xor_18_out, in_4, xor_11_out);
  and and_9 (and_9_out, xor_11_out, in_4);
  xor xor_19 (xor_19_out, in_21, xor_13_out);
  and and_10 (and_10_out, xor_13_out, in_21);
  xor xor_20 (xor_20_out, in_37, xor_15_out);
  and and_11 (and_11_out, xor_15_out, in_37);
  xor xor_21 (xor_21_out, in_53, xor_17_out);
  and and_12 (and_12_out, xor_17_out, in_53);
  and and_13 (and_13_out, xor_18_out, or_1_out);
  and and_14 (and_14_out, xor_19_out, or_2_out);
  and and_15 (and_15_out, xor_20_out, or_3_out);
  xor xor_22 (xor_22_out, in_2, in_10);
  xor xor_23 (xor_23_out, in_2, in_26);
  xor xor_24 (xor_24_out, in_2, in_42);
  and and_16 (and_16_out, xor_21_out, or_4_out);
  xor xor_25 (out_68, xor_18_out, or_1_out);
  or or_5 (or_5_out, and_13_out, and_9_out);
  xor xor_26 (out_76, xor_19_out, or_2_out);
  or or_6 (or_6_out, and_14_out, and_10_out);
  xor xor_27 (out_84, xor_20_out, or_3_out);
  or or_7 (or_7_out, and_15_out, and_11_out);
  xor xor_28 (out_92, xor_21_out, or_4_out);
  or or_8 (or_8_out, and_16_out, and_12_out);
  xor xor_29 (xor_29_out, in_2, in_58);
  xor xor_30 (xor_30_out, in_6, xor_22_out);
  and and_17 (and_17_out, xor_22_out, in_6);
  xor xor_31 (xor_31_out, in_22, xor_23_out);
  and and_18 (and_18_out, xor_23_out, in_22);
  xor xor_32 (xor_32_out, in_38, xor_24_out);
  and and_19 (and_19_out, xor_24_out, in_38);
  xor xor_33 (xor_33_out, in_54, xor_29_out);
  and and_20 (and_20_out, xor_29_out, in_54);
  and and_21 (and_21_out, xor_30_out, or_5_out);
  and and_22 (and_22_out, xor_31_out, or_6_out);
  and and_23 (and_23_out, xor_32_out, or_7_out);
  and and_24 (and_24_out, xor_33_out, or_8_out);
  xor xor_34 (out_69, xor_30_out, or_5_out);
  or or_9 (or_9_out, and_21_out, and_17_out);
  xor xor_35 (xor_35_out, in_2, in_12);
  xor xor_36 (out_77, xor_31_out, or_6_out);
  or or_10 (or_10_out, and_22_out, and_18_out);
  xor xor_37 (xor_37_out, in_2, in_28);
  xor xor_38 (out_85, xor_32_out, or_7_out);
  or or_11 (or_11_out, and_23_out, and_19_out);
  xor xor_39 (xor_39_out, in_2, in_44);
  xor xor_40 (out_93, xor_33_out, or_8_out);
  or or_12 (or_12_out, and_24_out, and_20_out);
  xor xor_41 (xor_41_out, in_2, in_60);
  xor xor_42 (xor_42_out, in_7, xor_35_out);
  and and_25 (and_25_out, xor_35_out, in_7);
  xor xor_43 (xor_43_out, in_23, xor_37_out);
  and and_26 (and_26_out, xor_37_out, in_23);
  xor xor_44 (xor_44_out, in_39, xor_39_out);
  and and_27 (and_27_out, xor_39_out, in_39);
  xor xor_45 (xor_45_out, in_55, xor_41_out);
  and and_28 (and_28_out, xor_41_out, in_55);
  and and_29 (and_29_out, xor_42_out, or_9_out);
  and and_30 (and_30_out, xor_43_out, or_10_out);
  and and_31 (and_31_out, xor_44_out, or_11_out);
  xor xor_46 (xor_46_out, in_2, in_14);
  and and_32 (and_32_out, xor_45_out, or_12_out);
  xor xor_47 (out_70, xor_42_out, or_9_out);
  or or_13 (or_13_out, and_29_out, and_25_out);
  xor xor_48 (out_78, xor_43_out, or_10_out);
  or or_14 (or_14_out, and_30_out, and_26_out);
  xor xor_49 (xor_49_out, in_2, in_30);
  xor xor_50 (out_86, xor_44_out, or_11_out);
  or or_15 (or_15_out, and_31_out, and_27_out);
  xor xor_51 (xor_51_out, in_2, in_46);
  xor xor_52 (out_94, xor_45_out, or_12_out);
  or or_16 (or_16_out, and_32_out, and_28_out);
  xor xor_53 (xor_53_out, in_2, in_62);
  xor xor_54 (xor_54_out, in_9, xor_46_out);
  and and_33 (and_33_out, xor_46_out, in_9);
  xor xor_55 (xor_55_out, in_25, xor_49_out);
  and and_34 (and_34_out, xor_49_out, in_25);
  xor xor_56 (xor_56_out, in_41, xor_51_out);
  and and_35 (and_35_out, xor_51_out, in_41);
  xor xor_57 (xor_57_out, in_57, xor_53_out);
  and and_36 (and_36_out, xor_53_out, in_57);
  and and_37 (and_37_out, xor_54_out, or_13_out);
  and and_38 (and_38_out, xor_55_out, or_14_out);
  and and_39 (and_39_out, xor_56_out, or_15_out);
  and and_40 (and_40_out, xor_57_out, or_16_out);
  xor xor_58 (out_71, xor_54_out, or_13_out);
  or or_17 (or_17_out, and_37_out, and_33_out);
  xor xor_59 (xor_59_out, in_15, in_2);
  xor xor_60 (out_79, xor_55_out, or_14_out);
  or or_18 (or_18_out, and_38_out, and_34_out);
  xor xor_61 (xor_61_out, in_31, in_2);
  xor xor_62 (out_87, xor_56_out, or_15_out);
  or or_19 (or_19_out, and_39_out, and_35_out);
  xor xor_63 (xor_63_out, in_47, in_2);
  xor xor_64 (out_95, xor_57_out, or_16_out);
  xor xor_65 (xor_65_out, in_63, in_2);
  or or_20 (or_20_out, and_40_out, and_36_out);
  xor xor_66 (xor_66_out, in_11, xor_59_out);
  and and_41 (and_41_out, xor_59_out, in_11);
  xor xor_67 (xor_67_out, in_27, xor_61_out);
  and and_42 (and_42_out, xor_61_out, in_27);
  xor xor_68 (xor_68_out, in_43, xor_63_out);
  and and_43 (and_43_out, xor_63_out, in_43);
  xor xor_69 (xor_69_out, in_59, xor_65_out);
  and and_44 (and_44_out, xor_65_out, in_59);
  and and_45 (and_45_out, xor_66_out, or_17_out);
  and and_46 (and_46_out, xor_67_out, or_18_out);
  and and_47 (and_47_out, xor_68_out, or_19_out);
  and and_48 (and_48_out, xor_69_out, or_20_out);
  xor xor_70 (out_72, xor_66_out, or_17_out);
  or or_21 (or_21_out, and_45_out, and_41_out);
  xor xor_71 (xor_71_out, in_2, in_17);
  xor xor_72 (out_80, xor_67_out, or_18_out);
  or or_22 (or_22_out, and_46_out, and_42_out);
  xor xor_73 (xor_73_out, in_2, in_33);
  xor xor_74 (out_88, xor_68_out, or_19_out);
  or or_23 (or_23_out, and_47_out, and_43_out);
  xor xor_75 (xor_75_out, in_2, in_49);
  xor xor_76 (out_96, xor_69_out, or_20_out);
  or or_24 (or_24_out, and_48_out, and_44_out);
  xor xor_77 (xor_77_out, in_2, in_65);
  xor xor_78 (xor_78_out, in_13, xor_71_out);
  and and_49 (and_49_out, xor_71_out, in_13);
  xor xor_79 (xor_79_out, in_29, xor_73_out);
  and and_50 (and_50_out, xor_73_out, in_29);
  xor xor_80 (xor_80_out, in_45, xor_75_out);
  and and_51 (and_51_out, xor_75_out, in_45);
  xor xor_81 (xor_81_out, in_61, xor_77_out);
  and and_52 (and_52_out, xor_77_out, in_61);
  and and_53 (and_53_out, xor_78_out, or_21_out);
  and and_54 (and_54_out, xor_79_out, or_22_out);
  and and_55 (and_55_out, xor_80_out, or_23_out);
  and and_56 (and_56_out, xor_81_out, or_24_out);
  xor xor_82 (out_73, xor_78_out, or_21_out);
  or or_25 (or_25_out, and_53_out, and_49_out);
  xor xor_83 (xor_83_out, in_2, in_18);
  xor xor_84 (out_81, xor_79_out, or_22_out);
  or or_26 (or_26_out, and_54_out, and_50_out);
  xor xor_85 (xor_85_out, in_2, in_34);
  xor xor_86 (out_89, xor_80_out, or_23_out);
  or or_27 (or_27_out, and_55_out, and_51_out);
  xor xor_87 (xor_87_out, in_2, in_50);
  xor xor_88 (out_97, xor_81_out, or_24_out);
  or or_28 (or_28_out, and_56_out, and_52_out);
  xor xor_89 (xor_89_out, in_2, in_66);
  xor xor_90 (xor_90_out, in_16, xor_83_out);
  and and_57 (and_57_out, xor_83_out, in_16);
  xor xor_91 (xor_91_out, in_32, xor_85_out);
  and and_58 (and_58_out, xor_85_out, in_32);
  xor xor_92 (xor_92_out, in_48, xor_87_out);
  and and_59 (and_59_out, xor_87_out, in_48);
  xor xor_93 (xor_93_out, in_64, xor_89_out);
  and and_60 (and_60_out, xor_89_out, in_64);
  and and_61 (and_61_out, xor_90_out, or_25_out);
  and and_62 (and_62_out, xor_91_out, or_26_out);
  and and_63 (and_63_out, xor_92_out, or_27_out);
  and and_64 (and_64_out, xor_93_out, or_28_out);
  xor xor_94 (out_74, xor_90_out, or_25_out);
  or or_29 (or_29_out, and_61_out, and_57_out);
  xor xor_95 (out_82, xor_91_out, or_26_out);
  or or_30 (or_30_out, and_62_out, and_58_out);
  xor xor_96 (out_90, xor_92_out, or_27_out);
  or or_31 (or_31_out, and_63_out, and_59_out);
  xor xor_97 (out_98, xor_93_out, or_28_out);
  or or_32 (out_99, and_64_out, and_60_out);
  xor xor_98 (out_100, out_99, or_28_out);
endmodule
